# Fritzing sketch piezo-buzzer (saved by Fritzing 0.9.3b)
breadboards: 1

parts:
  VCC1 = 4 x AAA Battery Mount
  Part1 = Photon
  J1 = Piezo Speaker

nets:
  N1: VCC1.-, Part1.GND
  N2: VCC1.+, Part1.VIN
  N3: Part1.D3, J1.pin2
  N4: Part1.3V3, J1.pin1

notes:
  tone() works on pins: D0, D1, D2, D3, A4, A5, WKP, RX, TX
  The buzzer does not have a polarity. Connect one side to a pin and the other to GND.
