# Fritzing sketch drv2605 (saved by Fritzing 0.9.3b)
breadboards: 1

parts:
  VCC1 = 4 x AAA Battery Mount
  Part1 = Photon
  Part2 = Adafruit DRV2605L [part_number="Adafruit #2305"]
  MOTOR1 = Vibration Motor

nets:
  GND: VCC1.-, Part1.GND, Part2.GND
  N1: VCC1.+, Part1.VIN
  N2: Part1.D0, Part2.SDA
  N3: Part1.D1, Part2.SCL
  3V3: Part1.3V3, Part2.VIN
  N4: Part2.OUT+, MOTOR1.NEG
  N5: Part2.OUT-, MOTOR1.POS

notes:
  D0 -> SDA
  D1 -> SCL

custom parts:
  Adafruit DRV2605L: The DRV2605 from TI is a fancy little motor driver. Rather than controlling a stepper motor or DC motor, its designed specifically for controlling haptic motors - buzzers and vibration motors. Normally one would just turn those kinds of motors on and off, but this driver has the ability to have various effects when driving a vibe motor. For example, ramping the vibration level up and down,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
  Vibration Motor: An eccentric vibration motor!
