# Fritzing sketch mma8451 (saved by Fritzing 0.9.3b)
breadboards: 1

parts:
  VCC1 = 4 x AAA Battery Mount
  Part1 = Photon
  Part3 = Adafruit MMA8451 Accelerometer [part_number="Adafruit #2019"]

nets:
  GND: VCC1.-, Part1.GND, Part3.GND
  N1: VCC1.+, Part1.VIN
  N2: Part1.D0, Part3.SDA
  N3: Part1.D1, Part3.SCL
  3V3: Part1.3V3, Part3.+3V3

notes:
  D0 -> SDA
  D1 -> SCL

custom parts:
  Adafruit MMA8451 Accelerometer: So many accelerometers and so little time! We've expanded our accelerometer selection even more with this high-precision and inexpensive MMA8451 Triple-Axis Accelerometer w/ 14-bit ADC. You can detect motion, tilt and basic orientation with a digital accelerometer - and the MMA8451 is a great accelerometer to start with. It has a wide usage range, from +-2g up to +-8g yet is easy to use with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
