# Fritzing sketch neopixels (saved by Fritzing 0.9.3b)
breadboards: 1

parts:
  VCC1 = 4 x AAA Battery Mount
  Part1 = Photon
  LED1 = RGB LED (com. cathode, rbg) [package="5 mm [THT]"]
  LED2 = RGB LED (com. cathode, rbg) [package="5 mm [THT]"]
  LED3 = RGB LED (com. cathode, rbg) [package="5 mm [THT]"]

nets:
  GND: VCC1.-, Part1.GND, LED1.GND, LED2.GND, LED3.GND
  N1: VCC1.+, Part1.VIN
  N2: Part1.D0, LED1.DATA_IN
  N3: Part1.3V3, LED1.+5, LED2.+5, LED3.+5
  N4: LED1.DATA_OUT, LED2.DATA_IN
  N5: LED2.DATA_OUT, LED3.DATA_IN

notes:
  5mm Neopixel Pinout
  1: Data IN (shortest)
  2: +V
  3: GND (longest)
  4: Data OUT

custom parts:
  RGB LED (com. cathode, rbg): A 5mm tri-color LED with red, green and blue inside. Pin order: red - com. cathode - blue - green
