# Fritzing sketch photocell (saved by Fritzing 0.9.3b)
breadboards: 1

parts:
  VCC1 = 4 x AAA Battery Mount
  Part1 = Photon
  R1 = Photocell (LDR) [package=THT]
  R2 = Resistor [tolerance=±5% resistance=10k package=THT]

nets:
  N1: VCC1.-, Part1.GND, R2.Pin_1
  N2: VCC1.+, Part1.VIN
  N3: Part1.A0, R1.pin_1, R2.Pin_0
  N4: Part1.3V3, R1.pin_0
