# Fritzing sketch passive-infrared-sensor (saved by Fritzing 0.9.3b)
breadboards: 1

parts:
  VCC1 = 4 x AAA Battery Mount
  Part1 = Photon
  PIR1 = PIR sensor

nets:
  GND: VCC1.-, Part1.GND, PIR1.GND
  N1: VCC1.+, Part1.VIN
  N2: Part1.D0, PIR1.SIG
  3V3: Part1.3V3, PIR1.VDD
