# Fritzing sketch TMP36 (saved by Fritzing 0.9.3b)
breadboards: 1

parts:
  VCC1 = 4 x AAA Battery Mount
  Part1 = Photon
  T1 = TMP36 Temperature Sensor [package="TO92 [THT]"]

nets:
  GND: VCC1.-, Part1.GND, T1.GND
  N1: VCC1.+, Part1.VIN
  N2: Part1.A0, T1.Vout
  N3: Part1.3V3, T1.+Vs
